# Fritzing sketch HMS-Nongfu (saved by Fritzing 0.8.7b)
circuit board: 8.46667cm x 5.64444cm
breadboards: 1

parts:
  Part1 = Arduino Uno (Rev3)
  J1 = Infrared Proximity Sensor
  J2 = Infrared Proximity Sensor
  J3 = Basic Servo

nets:
  N1: Part1.A0, J1.Vout
  N2: Part1.A1, J2.Vout
  N3: Part1.D9_PWM, J3.pulse
  GND: Part1.GND, J1.GND, J2.GND, J3.gnd
  VCC: Part1.5V, J1.Vcc, J2.Vcc, J3.vcc
